// Logisim project ModularArithmeticUnit.circ as structural Verilog
module _1bitAdder (
  input  A,
  input  B,
  input  Cin,
  output Cout,
  output Q
);

  wire nand_1_out, nand_2_out, nand_3_out, nand_5_out, nand_6_out, nand_7_out, nand_9_out, not_1_out,
       not_2_out, not_3_out;

  not not_1 (not_1_out, A);
  not not_2 (not_2_out, B);
  not not_3 (not_3_out, Cin);
  nand nand_1 (nand_1_out, not_1_out, not_2_out, Cin);
  nand nand_2 (nand_2_out, not_1_out, B, not_3_out);
  nand nand_3 (nand_3_out, A, B, Cin);
  nand nand_4 (Q, nand_1_out, nand_2_out, nand_3_out, nand_5_out);
  nand nand_5 (nand_5_out, A, not_2_out, not_3_out);
  nand nand_6 (nand_6_out, A, B);
  nand nand_7 (nand_7_out, B, Cin);
  nand nand_8 (Cout, nand_6_out, nand_7_out, nand_9_out);
  nand nand_9 (nand_9_out, A, Cin);
endmodule

module _8bitAdder (
  input  [7:0] A,
  input  [7:0] B,
  input  Cin,
  output Cout,
  output V,
  output [7:0] Q
);

  wire n1bitadder_2_cout, n1bitadder_3_cout, n1bitadder_4_cout, n1bitadder_5_cout, n1bitadder_6_cout,
       n1bitadder_7_cout, n1bitadder_8_cout;

  xor xor_1 (V, Cout, n1bitadder_2_cout);
  _1bitAdder u_1bitadder_1 (.A(A[7]), .B(B[7]), .Cin(n1bitadder_2_cout), .Q(Q[7]), .Cout(Cout));
  _1bitAdder u_1bitadder_2 (.A(A[6]), .B(B[6]), .Cin(n1bitadder_3_cout), .Q(Q[6]), .Cout(n1bitadder_2_cout));
  _1bitAdder u_1bitadder_3 (.A(A[5]), .B(B[5]), .Cin(n1bitadder_4_cout), .Q(Q[5]), .Cout(n1bitadder_3_cout));
  _1bitAdder u_1bitadder_4 (.A(A[4]), .B(B[4]), .Cin(n1bitadder_5_cout), .Q(Q[4]), .Cout(n1bitadder_4_cout));
  _1bitAdder u_1bitadder_5 (.A(A[3]), .B(B[3]), .Cin(n1bitadder_6_cout), .Q(Q[3]), .Cout(n1bitadder_5_cout));
  _1bitAdder u_1bitadder_6 (.A(A[2]), .B(B[2]), .Cin(n1bitadder_7_cout), .Q(Q[2]), .Cout(n1bitadder_6_cout));
  _1bitAdder u_1bitadder_7 (.A(A[1]), .B(B[1]), .Cin(n1bitadder_8_cout), .Q(Q[1]), .Cout(n1bitadder_7_cout));
  _1bitAdder u_1bitadder_8 (.A(A[0]), .B(B[0]), .Cin(Cin), .Q(Q[0]), .Cout(n1bitadder_8_cout));
endmodule

module ArithmeticUnit (
  input  Cin,
  input  [7:0] A,
  input  [7:0] B,
  input  [2:0] SEL_OP,
  output Cout,
  output V,
  output [7:0] Q
);

  wire multiplexer_3_out, not_3_out;
  wire [7:0] multiplexer_1_out, multiplexer_2_out, not_1_out, not_2_out;

  assign not_1_out = ~A;  // NOT_Gate not_1, 8 bits wide
  Multiplexer #(.select(3), .width(8), .enable("false")) multiplexer_1 (
    .in0(A), .in1(A), .in2(A), .in3(A), .in4(not_1_out), .in5(A), .in6(A), .in7({8{1'b0}}),
    .out(multiplexer_1_out), .sel(SEL_OP));
  assign not_2_out = ~B;  // NOT_Gate not_2, 8 bits wide
  Multiplexer #(.select(3), .width(8), .enable("false")) multiplexer_2 (
    .in0(B), .in1(B), .in2(8'h1), .in3({8{1'b1}}), .in4(8'h1), .in5(not_2_out), .in6(not_2_out), .in7(B),
    .out(multiplexer_2_out), .sel(SEL_OP));
  _8bitAdder u_8bitadder_1 (
    .A(multiplexer_1_out), .B(multiplexer_2_out), .Cout(Cout), .V(V), .Cin(multiplexer_3_out), .Q(Q));
  not not_3 (not_3_out, Cin);
  Multiplexer #(.select(3), .enable("false")) multiplexer_3 (
    .in0(1'b0), .in1(Cin), .in2(1'b0), .in3(1'b0), .in4(1'b0), .in5(1'b1), .in6(not_3_out), .in7(1'b0),
    .out(multiplexer_3_out), .sel(SEL_OP));
endmodule

module LogicUnit (
  input  Cin,
  input  [7:0] A,
  input  [7:0] B,
  input  [2:0] SEL_OP,
  output Cout,
  output [7:0] Q
);

  wire lsl_1_cout, lsr_1_cout, rol_1_cout, ror_1_cout;
  wire [7:0] AND_out, lsl_1_q, lsr_1_q, NOT_out, OR_out, rol_1_q, ror_1_q, XOR_out;

  assign OR_out = A | B;  // OR_Gate OR, 8 bits wide
  assign AND_out = A & B;  // AND_Gate AND, 8 bits wide
  assign XOR_out = A ^ B;  // XOR_Gate XOR, 8 bits wide
  Multiplexer #(.select(3), .width(8), .enable("false")) multiplexer_1 (
    .in0(AND_out), .in1(OR_out), .in2(XOR_out), .in3(NOT_out), .in4(lsl_1_q), .in5(lsr_1_q), .in6(rol_1_q),
    .in7(ror_1_q), .out(Q), .sel(SEL_OP));
  assign NOT_out = ~A;  // NOT_Gate NOT, 8 bits wide
  LSL lsl_1 (.Cout(lsl_1_cout), .A(A), .Q(lsl_1_q));
  LSR lsr_1 (.Cout(lsr_1_cout), .A(A), .Q(lsr_1_q));
  ROL rol_1 (.Cout(rol_1_cout), .A(A), .Ci(Cin), .Q(rol_1_q));
  Multiplexer #(.select(3), .enable("false")) multiplexer_2 (
    .in0(Cin), .in1(Cin), .in2(Cin), .in3(Cin), .in4(lsl_1_cout), .in5(lsr_1_cout), .in6(rol_1_cout),
    .in7(ror_1_cout), .out(Cout), .sel(SEL_OP));
  ROR ror_1 (.Ci(Cin), .Cout(ror_1_cout), .A(A), .Q(ror_1_q));
endmodule

module LSL (
  input  [7:0] A,
  output Cout,
  output [7:0] Q
);


  assign Cout = A[7];
  assign Q = {A[6:0], 1'b0};
endmodule

module LSR (
  input  [7:0] A,
  output Cout,
  output [7:0] Q
);


  assign Cout = A[0];
  assign Q = {1'b0, A[7:1]};
endmodule

module ROL (
  input  [7:0] A,
  input  Ci,
  output Cout,
  output [7:0] Q
);


  assign Cout = A[7];
  assign Q = {A[6:0], Ci};
endmodule

module ROR (
  input  [7:0] A,
  input  Ci,
  output Cout,
  output [7:0] Q
);


  assign Cout = A[0];
  assign Q = {Ci, A[7:1]};
endmodule

module ALU (
  input  [7:0] A,
  input  [7:0] B,
  input  [3:0] SREG_IN_VNZC,
  input  [3:0] OP_SEL,
  output [3:0] SREG_OUT_V,
  output [7:0] Q
);

  wire arithmeticunit_1_cout, arithmeticunit_1_v, logicunit_1_cout;
  wire [7:0] arithmeticunit_1_q, logicunit_1_q;

  ArithmeticUnit arithmeticunit_1 (
    .SEL_OP(OP_SEL[2:0]), .Cout(arithmeticunit_1_cout), .V(arithmeticunit_1_v), .A(A), .B(B),
    .Cin(SREG_IN_VNZC[0]), .Q(arithmeticunit_1_q));
  Multiplexer #(.width(8), .enable("false")) multiplexer_1 (
    .in0(arithmeticunit_1_q), .in1(logicunit_1_q), .out(Q), .sel(OP_SEL[3]));
  LogicUnit logicunit_1 (
    .SEL_OP(OP_SEL[2:0]), .Cout(logicunit_1_cout), .A(A), .B(B), .Cin(SREG_IN_VNZC[0]), .Q(logicunit_1_q));
  nor nor_1 (SREG_OUT_V[1], Q[7], Q[6], Q[5], Q[4], Q[3], Q[2], Q[1], Q[0]);
  Multiplexer #(.enable("false")) multiplexer_2 (
    .in0(arithmeticunit_1_cout), .in1(logicunit_1_cout), .out(SREG_OUT_V[0]), .sel(OP_SEL[3]));
  Multiplexer #(.enable("false")) multiplexer_3 (
    .in0(arithmeticunit_1_v), .in1(SREG_IN_VNZC[3]), .out(SREG_OUT_V[3]), .sel(OP_SEL[3]));

  assign SREG_OUT_V[2] = Q[7];

  // Notes on the sheet:
  //   0000 = ADD 
  //   0001 = ADC
  //   0010 = INC
  //   0011 = DEC
  //   0100 = NEG
  //   0101 = SUB
  //   0110 = SBC
  //   0111 = MOV
  //   1000 = AND
  //   1001 = OR
  //   1010 = XOR
  //   1011 = NOT
  //   1100 = LSL
  //   1101 = LSR
  //   1110 = ROL
  //   1111 = ROR
endmodule

module GPR (
  input  [7:0] dataW,
  input  [2:0] addW,
  input  reset,
  input  CLK_W,
  input  wEnGPR,
  input  [2:0] addA,
  input  [2:0] addB,
  output [7:0] A,
  output [7:0] B
);

  wire and_1_out, decoder_1_out0, decoder_1_out1, decoder_1_out2, decoder_1_out3, decoder_1_out4,
       decoder_1_out5, decoder_1_out6, decoder_1_out7;
  wire [7:0] R0_q, R1_q, R2_q, R3_q, R4_q, R5_q, R6_q, R7_q;

  Decoder #(.select(3), .enable("false")) decoder_1 (
    .out0(decoder_1_out0), .out1(decoder_1_out1), .out2(decoder_1_out2), .out3(decoder_1_out3),
    .out4(decoder_1_out4), .out5(decoder_1_out5), .out6(decoder_1_out6), .out7(decoder_1_out7), .sel(addW));
  and and_1 (and_1_out, CLK_W, wEnGPR);
  Register R0 (.D(dataW), .en(decoder_1_out0), .Q(R0_q), .clk(and_1_out), .clr(reset));
  Multiplexer #(.select(3), .width(8), .enable("false")) multiplexer_1 (
    .in0(R0_q), .in1(R1_q), .in2(R2_q), .in3(R3_q), .in4(R4_q), .in5(R5_q), .in6(R6_q), .in7(R7_q), .out(A),
    .sel(addA));
  Register R1 (.D(dataW), .en(decoder_1_out1), .Q(R1_q), .clk(and_1_out), .clr(reset));
  Register R4 (.D(dataW), .en(decoder_1_out4), .Q(R4_q), .clk(and_1_out), .clr(reset));
  Register R2 (.D(dataW), .en(decoder_1_out2), .Q(R2_q), .clk(and_1_out), .clr(reset));
  Register R5 (.D(dataW), .en(decoder_1_out5), .Q(R5_q), .clk(and_1_out), .clr(reset));
  Register R3 (.D(dataW), .en(decoder_1_out3), .Q(R3_q), .clk(and_1_out), .clr(reset));
  Register R6 (.D(dataW), .en(decoder_1_out6), .Q(R6_q), .clk(and_1_out), .clr(reset));
  Register R7 (.D(dataW), .en(decoder_1_out7), .Q(R7_q), .clk(and_1_out), .clr(reset));
  Multiplexer #(.select(3), .width(8), .enable("false")) multiplexer_2 (
    .in0(R0_q), .in1(R1_q), .in2(R2_q), .in3(R3_q), .in4(R4_q), .in5(R5_q), .in6(R6_q), .in7(R7_q), .out(B),
    .sel(addB));
endmodule

module ID (
  input  [15:0] Instruction,
  output [2:0] out_2,
  output [3:0] out_3,
  output [3:0] out_4,
  output [7:0] out_5,
  output [1:0] flag_sel,
  output flag_cmp,
  output [2:0] REG_A,
  output force_JMP,
  output rEn_RAM,
  output wEn_RAM,
  output en_JMP_BR,
  output sReg_wRn,
  output wEn_GPR,
  output [1:0] GPR_SS
);

  ROM #(.addrWidth(4)) rom_1 (
    .addr(Instruction[15:12]), .data({GPR_SS, wEn_GPR, sReg_wRn, en_JMP_BR, wEn_RAM, rEn_RAM, force_JMP}));  // open: sel

  assign flag_cmp = Instruction[10];
  assign flag_sel = Instruction[9:8];
  assign out_2 = Instruction[2:0];
  assign out_3 = Instruction[3:0];
  assign out_4 = Instruction[7:4];
  assign out_5 = Instruction[7:0];
  assign REG_A = Instruction[10:8];

  // Notes on the sheet:
  //   contents of rom_1 (hex, n*v repeats v):
  //   b0 10 20 62 4 9 8
endmodule

module CPUv_0 (
  input  [15:0] in_1,
  input  [7:0] valueFromRAM,
  input  RESET,
  input  CLOCK,
  output [3:0] adressRAM,
  output [7:0] dataToRAM,
  output wEn_RAM,
  output rEn_RAM,
  output [7:0] FLASH_ADDRESS
);

  wire id_1_en_jmp_br, id_1_flag_cmp, id_1_force_jmp, id_1_sreg_wrn, id_1_wen_gpr, multiplexer_2_out,
       multiplexer_4_out, not_1_out, or_1_out, xnor_1_out;
  wire [1:0] id_1_flag_sel, id_1_gpr_ss;
  wire [2:0] id_1_out_2, id_1_reg_a;
  wire [3:0] alu_1_sreg_out_v, id_1_out_4, register_2_q;
  wire [7:0] adder_1_out, alu_1_q, gpr_1_b, id_1_out_5, multiplexer_1_out, multiplexer_3_out;
  wire [15:0] register_1_q;

  ID id_1 (
    .out_2(id_1_out_2), .out_3(adressRAM), .out_4(id_1_out_4), .out_5(id_1_out_5), .flag_sel(id_1_flag_sel),
    .flag_cmp(id_1_flag_cmp), .REG_A(id_1_reg_a), .force_JMP(id_1_force_jmp), .rEn_RAM(rEn_RAM),
    .wEn_RAM(wEn_RAM), .en_JMP_BR(id_1_en_jmp_br), .sReg_wRn(id_1_sreg_wrn), .wEn_GPR(id_1_wen_gpr),
    .GPR_SS(id_1_gpr_ss), .Instruction(register_1_q));
  Register #(.width(16)) register_1 (.D(in_1), .en(1'b1), .Q(register_1_q), .clk(CLOCK));  // open: clr
  not not_1 (not_1_out, CLOCK);
  Adder adder_1 (.a(FLASH_ADDRESS), .b(8'h1), .out(adder_1_out), .cin(1'b0));  // open: cout
  Multiplexer #(.width(8), .enable("false")) multiplexer_1 (
    .in0(adder_1_out), .in1(id_1_out_5), .out(multiplexer_1_out), .sel(multiplexer_2_out));
  GPR gpr_1 (
    .addW(id_1_reg_a), .reset(RESET), .CLK_W(not_1_out), .wEnGPR(id_1_wen_gpr), .addA(id_1_reg_a),
    .addB(id_1_out_2), .dataW(multiplexer_3_out), .A(dataToRAM), .B(gpr_1_b));
  ALU alu_1 (
    .OP_SEL(id_1_out_4), .SREG_IN_VNZC(register_2_q), .SREG_OUT_V(alu_1_sreg_out_v), .A(dataToRAM),
    .B(gpr_1_b), .Q(alu_1_q));
  Register PC (.D(multiplexer_1_out), .en(1'b1), .Q(FLASH_ADDRESS), .clk(not_1_out), .clr(RESET));
  Multiplexer #(.enable("false")) multiplexer_2 (
    .in0(1'b0), .in1(or_1_out), .out(multiplexer_2_out), .sel(id_1_en_jmp_br));
  Multiplexer #(.select(2), .width(8), .enable("false")) multiplexer_3 (
    .in0(id_1_out_5), .in1(valueFromRAM), .in2(alu_1_q), .in3({4'b0000, register_2_q}),
    .out(multiplexer_3_out), .sel(id_1_gpr_ss));
  Register #(.width(4)) register_2 (
    .D(alu_1_sreg_out_v), .en(id_1_sreg_wrn), .Q(register_2_q), .clk(not_1_out), .clr(RESET));
  or or_1 (or_1_out, id_1_force_jmp, xnor_1_out);
  xnor xnor_1 (xnor_1_out, id_1_flag_cmp, multiplexer_4_out);
  Multiplexer #(.select(2), .enable("false")) multiplexer_4 (
    .in0(register_2_q[0]), .in1(register_2_q[1]), .in2(register_2_q[2]), .in3(register_2_q[3]),
    .out(multiplexer_4_out), .sel(id_1_flag_sel));
endmodule

module MPU (
  input  in_1
);

  wire clock_1_out, cpuv_0_1_ren_ram, cpuv_0_1_wen_ram, not_1_out, or_1_out, RESET_out;
  wire [3:0] cpuv_0_1_adressram;
  wire [7:0] cpuv_0_1_datatoram, cpuv_0_1_flash_address, ram_1_data;
  wire [15:0] rom_1_data;

  ROM #(.dataWidth(16)) rom_1 (.addr(cpuv_0_1_flash_address), .data(rom_1_data));  // open: sel
  Clock clock_1 (.out(clock_1_out));
  CPUv_0 cpuv_0_1 (
    .in_1(rom_1_data), .wEn_RAM(cpuv_0_1_wen_ram), .rEn_RAM(cpuv_0_1_ren_ram),
    .FLASH_ADDRESS(cpuv_0_1_flash_address), .adressRAM(cpuv_0_1_adressram), .valueFromRAM(ram_1_data),
    .dataToRAM(cpuv_0_1_datatoram), .CLOCK(clock_1_out), .RESET(RESET_out));
  Button RESET (.out(RESET_out));
  not not_1 (not_1_out, clock_1_out);
  or or_1 (or_1_out, cpuv_0_1_wen_ram, cpuv_0_1_ren_ram);
  RAM #(.addrWidth(4), .bus("separate")) ram_1 (
    .addr(cpuv_0_1_adressram), .din(cpuv_0_1_datatoram), .data(ram_1_data), .str(cpuv_0_1_wen_ram),
    .sel(or_1_out), .clk(not_1_out), .ld(cpuv_0_1_ren_ram), .clr(in_1));

  // Notes on the sheet:
  //   contents of rom_1 (hex, n*v repeats v):
  //   2000 3000 3101 2200 2300 2400 90 650f 40 600c 311 6009 420 412 600c 110 212 5006 4302 4403 5014
endmodule
